# Fritzing sketch carro-joystick (saved by Fritzing 0.9.3b)
breadboards: 1

parts:
  L298N1 = L298N DC motor driver
  M2 = DC Motor  # not connected
  M3 = DC Motor  # not connected
  Part1 = Bluetooth HC-06
  Part2 = Arduino Uno (Rev3)
  VCC2 = 4 x AAA Battery Mount
  VCC3 = Battery block 9V  # not connected
  R1 = Resistor [tolerance=±5% resistance=22k package=THT]
  R2 = Resistor [tolerance=±5% resistance=10k package=THT]

nets:
  N1: L298N1.IN1, Part2.D5_PWM
  N2: L298N1.IN2, Part2.D6_PWM
  N3: L298N1.IN3, Part2.D9_PWM
  N4: L298N1.IN4, Part2.D10_PWM/SS
  N5: Part1.RXD, R1.Pin_0, R2.Pin_1
  N6: Part1.TXD, Part2.D0/RX
  N7: Part1.GND, R1.Pin_1
  N8: Part2.GND, VCC2.-
  N9: Part2.D1/TX, R2.Pin_0

custom parts:
  L298N DC motor driver: 2x DC motor driver with 78M05 positive voltage regulator (7..35 V) L298N: max 46 V, 2 A Set 5 V Enable jumper to enable 5 V regultor (needed for the L298N) and +5 V output at screw terminal or supply external +5 V at screw terminal Set ENA and/or ENB to +5 V to enable motor permanently or supply ENA and/or ENB with PWM signal IN1 and IN2 set rotation directory for motor A (OUT1/OUT2) IN2 and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
