# Fritzing sketch dado (saved by Fritzing 0.9.3b)
breadboards: 1

parts:
  DI1 = 7-Segment LED Display [package=THT]
  R1 = Resistor [tolerance=±5% resistance=1k package=THT]
  R2 = Resistor [tolerance=±5% resistance=1k package=THT]
  R3 = Resistor [tolerance=±5% resistance=1k package=THT]
  R4 = Resistor [tolerance=±5% resistance=1k package=THT]
  R5 = Resistor [tolerance=±5% resistance=1k package=THT]
  R6 = Resistor [tolerance=±5% resistance=1k package=THT]
  R7 = Resistor [tolerance=±5% resistance=1k package=THT]
  R8 = Resistor [tolerance=±5% resistance=1k package=THT]
  S1 = Pushbutton [package="[THT]"]
  Part1 = Arduino Uno (Rev3)

nets:
  N1: DI1.cathodeE, R8.Pin_1
  N2: DI1.cathodeD, R7.Pin_1
  N3: DI1.commAnode#2, S1.Pin_3, S1.Pin_4, Part1.GND
  N4: DI1.cathodeC, R5.Pin_1
  N5: DI1.cathodeDP, R6.Pin_1
  N6: DI1.cathodeB, R4.Pin_1
  N7: DI1.cathodeA, R3.Pin_1
  N8: DI1.cathodeF, R1.Pin_1
  N9: DI1.cathodeG, R2.Pin_1
  N10: R1.Pin_0, Part1.D11_PWM/MOSI
  N11: R2.Pin_0, Part1.D12/MISO
  N12: R3.Pin_0, Part1.D10_PWM/SS
  N13: R4.Pin_0, Part1.D9_PWM
  N14: R5.Pin_0, Part1.D5_PWM
  N15: R6.Pin_0, Part1.D4
  N16: R7.Pin_0, Part1.D6_PWM
  N17: R8.Pin_0, Part1.D7
  N18: S1.Pin_1, S1.Pin_2, Part1.D13/SCK
