# Fritzing sketch genius (saved by Fritzing 0.9.3b)
breadboards: 1

parts:
  R1 = Resistor [tolerance=±5% resistance=220 package=THT]
  LED1 = LED - 5mm [color="Red (633nm)" package="5 mm [THT]"]
  S1 = Pushbutton [package="[THT]"]
  R3 = Resistor [tolerance=±5% resistance=220 package=THT]
  LED3 = LED - 5mm [color="Green (570nm)" package="5 mm [THT]"]
  S3 = Pushbutton [package="[THT]"]
  R4 = Resistor [tolerance=±5% resistance=220 package=THT]
  LED4 = LED - 5mm [color="Yellow (595nm)" package="5 mm [THT]"]
  S4 = Pushbutton [package="[THT]"]
  R5 = Resistor [tolerance=±5% resistance=220 package=THT]
  LED5 = LED - 5mm [color="Blue (430nm)" package="5 mm [THT]"]  # not connected
  S5 = Pushbutton [package="[THT]"]
  J1 = Piezo Speaker
  Part1 = Arduino Uno (Rev3)

nets:
  N1: R1.Pin_0, S1.Pin_1, S1.Pin_2, S3.Pin_1, S3.Pin_2, R4.Pin_0, S4.Pin_1, S4.Pin_2, R5.Pin_0, S5.Pin_1, S5.Pin_2, J1.pin1, Part1.GND
  N2: R1.Pin_1, LED1.cathode
  N3: LED1.anode, Part1.D2
  N4: S1.Pin_3, S1.Pin_4, Part1.D3_PWM
  N5: R3.Pin_1, LED3.cathode
  N6: LED3.anode, Part1.D4
  N7: S3.Pin_3, S3.Pin_4, Part1.D5_PWM
  N8: R4.Pin_1, LED4.cathode
  N9: LED4.anode, Part1.D6_PWM
  N10: S4.Pin_3, S4.Pin_4, Part1.D7
  N11: S5.Pin_3, S5.Pin_4, Part1.D9_PWM
  N12: J1.pin2, Part1.D12/MISO
