# Fritzing sketch potenciometro-1 (saved by Fritzing 0.9.3b)
breadboards: 1

parts:
  Part1 = Arduino Uno (Rev3)
  R1 = Resistor [tolerance=±5% resistance=220 package=THT]
  R2 = Resistor [tolerance=±5% resistance=220 package=THT]
  R3 = Resistor [tolerance=±5% resistance=220 package=THT]
  R4 = Resistor [tolerance=±5% resistance=220 package=THT]
  R5 = Resistor [tolerance=±5% resistance=220 package=THT]
  R6 = Resistor [tolerance=±5% resistance=220 package=THT]
  LED1 = LED - 5mm [color="Red (633nm)" package="5 mm [THT]"]
  LED2 = LED - 5mm [color="Orange (620nm)" package="5 mm [THT]"]
  LED3 = LED - 5mm [color="Yellow (595nm)" package="5 mm [THT]"]
  LED4 = LED - 5mm [color="Green (570nm)" package="5 mm [THT]"]
  LED5 = LED - 5mm [color="Blue (525nm)" package="5 mm [THT]"]
  LED6 = LED - 5mm [color="White (4500K)" package="5 mm [THT]"]
  R7 = Rotary Potentiometer (Small) [maximum_resistance=100kΩ package=THT]

nets:
  N1: Part1.A0, R7.wiper
  N2: Part1.D8, LED1.anode
  N3: Part1.D9_PWM, LED2.anode
  N4: Part1.D10_PWM/SS, LED3.anode
  N5: Part1.D11_PWM/MOSI, LED4.anode
  N6: Part1.D12/MISO, LED5.anode
  N7: Part1.D13/SCK, LED6.anode
  N8: Part1.5V, R7.leg2
  N9: R1.Pin_0, R2.Pin_0, R3.Pin_0, R4.Pin_0, R5.Pin_0, R6.Pin_0, R7.leg1
  N10: R1.Pin_1, LED1.cathode
  N11: R2.Pin_1, LED2.cathode
  N12: R3.Pin_1, LED4.cathode
  N13: R4.Pin_1, LED3.cathode
  N14: R5.Pin_1, LED5.cathode
  N15: R6.Pin_1, LED6.cathode
